// Logisim project A1_Group3.circ as structural Verilog: 1 circuit, main circuit main
module main (
  input  [31:0] Input_A,
  input  [31:0] Input_B,
  output UNDERFLOW,
  output OVERFLOW,
  output [31:0] OUTPUT
);

  wire Exp__Normalizer_2_overflow, Exp__Normalizer_2_underflow, Exp__Normalizer_overflow,
       Exp__Normalizer_underflow, multiplexer_1_out, or_3_out, Preprocessor_sign_a, Preprocessor_sign_b,
       Rounder_cout, Signif__Adder_cout;
  wire [4:0] Signifi__Normalizer_left_shamt, Signifi_Normalizer_left_shamt;
  wire [10:0] Exp__Normalizer_exponent_result, Preprocessor_greater_exponent_exp_a;
  wire [31:0] Preprocessor_frac_a__converted_into_32_bits, Preprocessor_shifted_frac_b,
       Rounder_rounded_32_bit_significand, Signif__Adder_significand_to_be_shifted,
       Signifi__Normalizer_normalized_32_bit_significand, Signifi_Normalizer_normalized_32_bit_significand;

  Multiplexer #(.enable("false")) multiplexer_1 (
    .in0(Preprocessor_sign_b), .in1(Preprocessor_sign_a), .out(multiplexer_1_out), .sel(Signif__Adder_cout));
  Preprocessor_Circuit Preprocessor (
    .Input_A(Input_A), .Input_B(Input_B), .Greater_exponent_exp_A(Preprocessor_greater_exponent_exp_a),
    .Sign_A(Preprocessor_sign_a), .Sign_B(Preprocessor_sign_b), .shifted_frac_B(Preprocessor_shifted_frac_b),
    .frac_A__converted_into_32_bits(Preprocessor_frac_a__converted_into_32_bits));  // open: Lesser_Exponent_exp_B, Shamt
  Exponent_Normalization Exp__Normalizer (
    .NORMALIZED_32_BIT_SIGNIFICAND(Signifi_Normalizer_normalized_32_bit_significand),
    .GREATER_EXPONENT(Preprocessor_greater_exponent_exp_a),
    .LEFT_SHAMT_FROM_FRACNORM(Signifi_Normalizer_left_shamt), .Cin_of_Final_Adder(Signif__Adder_cout),
    .EXPONENT_RESULT(Exp__Normalizer_exponent_result), .OVERFLOW(Exp__Normalizer_overflow),
    .UNDERFLOW(Exp__Normalizer_underflow));
  or or_1 (OVERFLOW, Exp__Normalizer_overflow, Exp__Normalizer_2_overflow);
  or or_2 (UNDERFLOW, Exp__Normalizer_underflow, Exp__Normalizer_2_underflow);
  Significant_Adder Signif__Adder (
    .Sign_A(Preprocessor_sign_a), .Sign_B(Preprocessor_sign_b), .frac_B(Preprocessor_shifted_frac_b),
    .frac_A(Preprocessor_frac_a__converted_into_32_bits),
    .Significand_to_be_Shifted(Signif__Adder_significand_to_be_shifted), .Cout(Signif__Adder_cout));
  FractionNormalization Signifi_Normalizer (
    .Significand_to_be_Shifted(Signif__Adder_significand_to_be_shifted), .Cout(Signif__Adder_cout),
    .Normalized_32_bit_Significand(Signifi_Normalizer_normalized_32_bit_significand),
    .LEFT_SHAMT(Signifi_Normalizer_left_shamt));
  Exponent_Normalization Exp__Normalizer_2 (
    .NORMALIZED_32_BIT_SIGNIFICAND({Signifi__Normalizer_normalized_32_bit_significand[31], OUTPUT[19:0], Signifi__Normalizer_normalized_32_bit_significand[10:0]}),
    .GREATER_EXPONENT(Exp__Normalizer_exponent_result),
    .LEFT_SHAMT_FROM_FRACNORM(Signifi__Normalizer_left_shamt), .Cin_of_Final_Adder(Rounder_cout),
    .EXPONENT_RESULT(OUTPUT[30:20]), .OVERFLOW(Exp__Normalizer_2_overflow),
    .UNDERFLOW(Exp__Normalizer_2_underflow));
  Rounding_Circuit Rounder (
    .Normalized_32_bit_Significand(Signifi_Normalizer_normalized_32_bit_significand),
    .Rounded_32_bit_Significand(Rounder_rounded_32_bit_significand), .Cout(Rounder_cout));
  FractionNormalization Signifi__Normalizer (
    .Significand_to_be_Shifted(Rounder_rounded_32_bit_significand), .Cout(Rounder_cout),
    .Normalized_32_bit_Significand({Signifi__Normalizer_normalized_32_bit_significand[31], OUTPUT[19:0], Signifi__Normalizer_normalized_32_bit_significand[10:0]}),
    .LEFT_SHAMT(Signifi__Normalizer_left_shamt));
  or or_3 (or_3_out, OUTPUT[0], OUTPUT[1], OUTPUT[2], OUTPUT[3], OUTPUT[4], OUTPUT[5], OUTPUT[6], OUTPUT[7], OUTPUT[8], OUTPUT[9], OUTPUT[11], OUTPUT[12], OUTPUT[13], OUTPUT[14], OUTPUT[15], OUTPUT[16], OUTPUT[17], OUTPUT[18], OUTPUT[19], OUTPUT[10]);
  Multiplexer #(.enable("false")) multiplexer_2 (.in0(1'b0), .in1(multiplexer_1_out), .out(OUTPUT[31]), .sel(or_3_out));
endmodule
