// Logisim project A1_Group3.circ as structural Verilog: 1 circuit, main circuit main
module main (
  input  A0,
  input  A1,
  input  A2,
  input  A3,
  input  B0,
  input  B1,
  input  B2,
  input  B3,
  input  in_9,
  input  in_10,
  input  in_11,
  output S0,
  output S1,
  output S2,
  output S3,
  output Cout,
  output C,
  output V,
  output S,
  output Z
);

  wire n7404_1__2__1y, n7404_1__4__2y, n7404_1__6__3y, n7404_1__8__4y, n7404_1__10__5y, n7404_1__12__6y,
       n7404_2__2__1y, n7404_2__4__2y, n7404_2__6__3y, n7404_2__12__6y, n7408_1__3__1y, n7408_1__6__2y,
       n7408_1__8__3y, n7408_1__11__4y, n7408_2__3__1y, n7408_2__6__2y, n7408_2__8__3y, n7408_2__11__4y,
       n7432_1__3__1y, n7432_1__6__2y, n7432_1__8__3y, n7432_1__11__4y, n7432_2__3__1y, n7432_2__6__2y,
       n7432_2__8__3y, n7432_3__8__3y, n7432_3__11__4y, n7486_1__3__1y, n7486_1__6__2y, n7486_1__8__3y,
       n74153_1__7__y1, n74153_1__9__y2, n74153_2__7__y1, n74153_2__9__y2, n74153_3__7__y1, n74153_3__9__y2,
       n74153_4__7__y1, n74153_4__9__y2, n74157_1__4__y1, n74157_1__7__y2, n74157_1__9__y3, n74157_1__12__y4;

  _7404 u_7404_1 (
    ._1__1A(A0), ._2__1Y(n7404_1__2__1y), ._3__2A(B0), ._4__2Y(n7404_1__4__2y), ._5__3A(A1),
    ._6__3Y(n7404_1__6__3y), ._7__GND(1'b0), ._14__Vcc(1'b1), ._13__6A(B1), ._12__6Y(n7404_1__12__6y),
    ._11__5A(A2), ._10__5Y(n7404_1__10__5y), ._9__4A(B2), ._8__4Y(n7404_1__8__4y));
  _7408 u_7408_1 (
    ._1__1A(n7404_1__2__1y), ._2__1B(B0), ._3__1Y(n7408_1__3__1y), ._4__2A(n7404_1__6__3y), ._5__2B(B1),
    ._6__2Y(n7408_1__6__2y), ._7__GND(1'b0), ._14__Vcc(1'b1), ._13__4B(n7404_1__10__5y), ._12__4A(B2),
    ._11__4Y(n7408_1__11__4y), ._10__3B(n7404_2__2__1y), ._9__3A(B3), ._8__3Y(n7408_1__8__3y));
  _7432 u_7432_1 (
    ._1__1A(n7404_1__2__1y), ._2__1B(B0), ._3__1Y(n7432_1__3__1y), ._4__2A(n7404_1__6__3y), ._5__2B(B1),
    ._6__2Y(n7432_1__6__2y), ._7__GND(1'b0), ._14__Vcc(1'b1), ._13__4B(n7404_1__10__5y), ._12__4A(B2),
    ._11__4Y(n7432_1__11__4y), ._10__3B(n7404_2__2__1y), ._9__3A(B3), ._8__3Y(n7432_1__8__3y));
  _7404 u_7404_2 (
    ._1__1A(A3), ._2__1Y(n7404_2__2__1y), ._3__2A(B3), ._4__2Y(n7404_2__4__2y), ._5__3A(in_9),
    ._6__3Y(n7404_2__6__3y), ._7__GND(1'b0), ._14__Vcc(1'b1), ._13__6A(in_10), ._12__6Y(n7404_2__12__6y),
    ._11__5A(n7432_2__8__3y), ._10__5Y(Z));  // open: _9__4A, _8__4Y
  _74153 u_74153_1 (
    ._1__nG1(1'b0), ._2__B(in_10), ._3__1C3(n7404_1__4__2y), ._4__1C2(n7404_1__4__2y), ._5__1C1(1'b0),
    ._6__1C0(n7404_1__4__2y), ._7__Y1(n74153_1__7__y1), ._8__GND(1'b0), ._16__Vcc(1'b1), ._15__nG2(1'b0),
    ._14__A(in_11), ._13__2C3(n7408_1__3__1y), ._12__2C2(n7408_1__3__1y), ._11__2C1(n7432_1__3__1y),
    ._10__2C0(1'b0), ._9__Y2(n74153_1__9__y2));
  _74153 u_74153_2 (
    ._1__nG1(1'b0), ._2__B(in_10), ._3__1C3(n7404_1__12__6y), ._4__1C2(n7404_1__12__6y), ._5__1C1(1'b0),
    ._6__1C0(n7404_1__12__6y), ._7__Y1(n74153_2__7__y1), ._8__GND(1'b0), ._16__Vcc(1'b1), ._15__nG2(1'b0),
    ._14__A(in_11), ._13__2C3(n7408_1__6__2y), ._12__2C2(n7408_1__6__2y), ._11__2C1(n7432_1__6__2y),
    ._10__2C0(1'b0), ._9__Y2(n74153_2__9__y2));
  _74153 u_74153_3 (
    ._1__nG1(1'b0), ._2__B(in_10), ._3__1C3(n7404_1__8__4y), ._4__1C2(n7404_1__8__4y), ._5__1C1(1'b0),
    ._6__1C0(n7404_1__8__4y), ._7__Y1(n74153_3__7__y1), ._8__GND(1'b0), ._16__Vcc(1'b1), ._15__nG2(1'b0),
    ._14__A(in_11), ._13__2C3(n7408_1__11__4y), ._12__2C2(n7408_1__11__4y), ._11__2C1(n7432_1__11__4y),
    ._10__2C0(1'b0), ._9__Y2(n74153_3__9__y2));
  _74153 u_74153_4 (
    ._1__nG1(1'b0), ._2__B(in_10), ._3__1C3(n7404_2__4__2y), ._4__1C2(n7404_2__4__2y), ._5__1C1(1'b0),
    ._6__1C0(n7404_2__4__2y), ._7__Y1(n74153_4__7__y1), ._8__GND(1'b0), ._16__Vcc(1'b1), ._15__nG2(1'b0),
    ._14__A(in_11), ._13__2C3(n7408_1__8__3y), ._12__2C2(n7408_1__8__3y), ._11__2C1(n7432_1__8__3y),
    ._10__2C0(1'b0), ._9__Y2(n74153_4__9__y2));
  _74157 u_74157_1 (
    ._1__S(in_9), ._2__A1(n74153_1__7__y1), ._3__B1(n74153_1__9__y2), ._4__Y1(n74157_1__4__y1),
    ._5__A2(n74153_2__7__y1), ._6__B2(n74153_2__9__y2), ._7__Y2(n74157_1__7__y2), ._8__GND(1'b0),
    ._16__Vcc(1'b1), ._15__G(1'b0), ._14__A4(n74153_3__7__y1), ._13__B4(n74153_3__9__y2),
    ._12__Y4(n74157_1__12__y4), ._11__A3(n74153_4__7__y1), ._10__B3(n74153_4__9__y2), ._9__Y3(n74157_1__9__y3));
  _7486 u_7486_1 (
    ._1__1A(A3), ._2__1B(n74157_1__9__y3), ._3__1Y(n7486_1__3__1y), ._4__2A(n7486_1__3__1y), ._5__2B(S),
    ._6__2Y(n7486_1__6__2y), ._7__GND(1'b0), ._14__Vcc(1'b1), ._10__3B(n7486_1__6__2y), ._9__3A(Cout),
    ._8__3Y(n7486_1__8__3y));  // open: _13__4B, _12__4A, _11__4Y
  _7483 u_7483_1 (
    ._1__A4(A3), ._2__S3(S2), ._3__A3(A2), ._4__B3(n74157_1__12__y4), ._5__Vcc(1'b1), ._6__S2(S1),
    ._7__B2(n74157_1__7__y2), ._8__A2(A1), ._16__B4(n74157_1__9__y3), ._15__S4(S), ._14__Cout(Cout),
    ._13__Cin(n7432_2__3__1y), ._12__GND(1'b0), ._11__B1(n74157_1__4__y1), ._10__A1(A0), ._9__S1(S0));
  _7408 u_7408_2 (
    ._1__1A(n7404_2__6__3y), ._2__1B(in_10), ._3__1Y(n7408_2__3__1y), ._4__2A(n7408_2__3__1y),
    ._5__2B(in_11), ._6__2Y(n7408_2__6__2y), ._7__GND(1'b0), ._14__Vcc(1'b1), ._13__4B(in_9),
    ._12__4A(n7404_2__12__6y), ._11__4Y(n7408_2__11__4y), ._10__3B(n7432_2__6__2y), ._9__3A(in_9),
    ._8__3Y(n7408_2__8__3y));
  _7432 u_7432_2 (
    ._1__1A(n7408_2__6__2y), ._2__1B(n7408_2__11__4y), ._3__1Y(n7432_2__3__1y), ._4__2A(in_10),
    ._5__2B(in_11), ._6__2Y(n7432_2__6__2y), ._7__GND(1'b0), ._14__Vcc(1'b1), ._10__3B(n7432_3__8__3y),
    ._9__3A(S), ._8__3Y(n7432_2__8__3y));  // open: _13__4B, _12__4A, _11__4Y
  _74157 u_74157_2 (
    ._1__S(n7408_2__8__3y), ._2__A1(n7486_1__8__3y), ._3__B1(1'b0), ._4__Y1(V), ._5__A2(Cout), ._6__B2(1'b0),
    ._7__Y2(C), ._8__GND(1'b0), ._16__Vcc(1'b1), ._15__G(1'b0));  // open: _14__A4, _13__B4, _12__Y4, _11__A3, _10__B3, _9__Y3
  _7432 u_7432_3 (
    ._7__GND(1'b0), ._14__Vcc(1'b1), ._13__4B(S0), ._12__4A(S1), ._11__4Y(n7432_3__11__4y),
    ._10__3B(n7432_3__11__4y), ._9__3A(S2), ._8__3Y(n7432_3__8__3y));  // open: _1__1A, _2__1B, _3__1Y, _4__2A, _5__2B, _6__2Y

  assign S3 = S;

  // Notes on the sheet:
  //   C2
  //   C1
  //   C0
  //   A0
  //   A1
  //   A2
  //   A3
  //   Y0
  //   Y1
  //   Y2
  //   Y3
  //   C2'
  //   GND
  //   Vcc
  //   C1'
  //   Cin
  //   CSE 306
  //   4-bit ALU Implementation
  //   Lab group: A1 - G3
endmodule
