// Logisim project PreprocessorCkt.circ as structural Verilog: 1 circuit, main circuit Preprocessor Circuit
module Preprocessor_Circuit (
  input  [31:0] Input_A,
  input  [31:0] Input_B,
  output [4:0] Shamt,
  output [10:0] Greater_exponent_exp_A,
  output [10:0] Lesser_Exponent_exp_B,
  output [31:0] shifted_frac_B,
  output [31:0] frac_A__converted_into_32_bits,
  output Sign_A,
  output Sign_B
);

  wire adder_1_cout, or_1_out;
  wire [10:0] adder_1_out, adder_2_out, multiplexer_7_out, not_1_out, not_2_out;
  wire [19:0] multiplexer_5_out;

  Multiplexer #(.width(11), .enable("false")) multiplexer_1 (
    .in0(Input_B[30:20]), .in1(Input_A[30:20]), .out(Greater_exponent_exp_A), .sel(adder_1_cout));
  Adder #(.width(11)) adder_1 (.a(Input_A[30:20]), .b(not_1_out), .out(adder_1_out), .cin(1'b1), .cout(adder_1_cout));
  Multiplexer #(.width(20), .enable("false")) multiplexer_2 (
    .in0(Input_B[19:0]), .in1(Input_A[19:0]), .out(frac_A__converted_into_32_bits[30:11]), .sel(adder_1_cout));
  Multiplexer #(.enable("false")) multiplexer_3 (
    .in0(Input_B[31]), .in1(Input_A[31]), .out(Sign_A), .sel(adder_1_cout));
  Multiplexer #(.width(11), .enable("false")) multiplexer_4 (
    .in0(Input_A[30:20]), .in1(Input_B[30:20]), .out(Lesser_Exponent_exp_B), .sel(adder_1_cout));
  Multiplexer #(.width(20), .enable("false")) multiplexer_5 (
    .in0(Input_A[19:0]), .in1(Input_B[19:0]), .out(multiplexer_5_out), .sel(adder_1_cout));
  Multiplexer #(.enable("false")) multiplexer_6 (
    .in0(Input_A[31]), .in1(Input_B[31]), .out(Sign_B), .sel(adder_1_cout));
  assign not_1_out = ~Input_B[30:20];  // NOT_Gate not_1, 11 bits wide
  assign not_2_out = ~adder_1_out;  // NOT_Gate not_2, 11 bits wide
  Multiplexer #(.width(11), .enable("false")) multiplexer_7 (
    .in0(adder_2_out), .in1(adder_1_out), .out(multiplexer_7_out), .sel(adder_1_cout));
  Adder #(.width(11)) adder_2 (.a({11{1'b0}}), .b(not_2_out), .out(adder_2_out), .cin(1'b1));  // open: cout
  or or_1 (or_1_out, multiplexer_7_out[10], multiplexer_7_out[9], multiplexer_7_out[8], multiplexer_7_out[7], multiplexer_7_out[6], multiplexer_7_out[5]);
  Multiplexer #(.width(5), .enable("false")) multiplexer_8 (
    .in0(multiplexer_7_out[4:0]), .in1({5{1'b1}}), .out(Shamt), .sel(or_1_out));
  Shifter #(.width(32), .shift("lr")) shifter_1 (
    .in({1'b1, multiplexer_5_out, {11{1'b0}}}), .\dist (Shamt), .out(shifted_frac_B));

  assign {frac_A__converted_into_32_bits[31], frac_A__converted_into_32_bits[10:0]} = 12'h800;

  // Notes on the sheet:
  //   Greater Fraction (A as per our definition)
  //   Lesser fraction (B as per our definition)
  //   frac(B) converted into 32 bits
endmodule
