// Logisim project FractionNormalization.circ as structural Verilog: 1 circuit, main circuit FractionNormalization
module FractionNormalization (
  input  [31:0] Significand_to_be_Shifted,
  input  [4:0] in_2,
  input  Cout,
  input  [3:0] in_4,
  output [31:0] Normalized_32_bit_Significand,
  output [4:0] out_6
);

  wire not_1_out;
  wire [4:0] multiplexer_1_out, not_2_out, priority_encoder_1_out;
  wire [31:0] shifter_1_out, shifter_2_out;

  Priority_Encoder #(.select(5)) priority_encoder_1 (
    .in0(Significand_to_be_Shifted[0]), .in1(Significand_to_be_Shifted[1]),
    .in2(Significand_to_be_Shifted[2]), .in3(Significand_to_be_Shifted[3]),
    .in4(Significand_to_be_Shifted[4]), .in5(Significand_to_be_Shifted[5]),
    .in6(Significand_to_be_Shifted[6]), .in7(Significand_to_be_Shifted[7]),
    .in8(Significand_to_be_Shifted[8]), .in9(Significand_to_be_Shifted[9]),
    .in10(Significand_to_be_Shifted[10]), .in11(Significand_to_be_Shifted[11]),
    .in12(Significand_to_be_Shifted[12]), .in13(Significand_to_be_Shifted[13]),
    .in14(Significand_to_be_Shifted[14]), .in15(Significand_to_be_Shifted[15]),
    .in16(Significand_to_be_Shifted[16]), .in17(Significand_to_be_Shifted[17]),
    .in18(Significand_to_be_Shifted[18]), .in19(Significand_to_be_Shifted[19]),
    .in20(Significand_to_be_Shifted[20]), .in21(Significand_to_be_Shifted[21]),
    .in22(Significand_to_be_Shifted[22]), .in23(Significand_to_be_Shifted[23]),
    .in24(Significand_to_be_Shifted[24]), .in25(Significand_to_be_Shifted[25]),
    .in26(Significand_to_be_Shifted[26]), .in27(Significand_to_be_Shifted[27]),
    .in28(Significand_to_be_Shifted[28]), .in29(Significand_to_be_Shifted[29]),
    .in30(Significand_to_be_Shifted[30]), .in31(Significand_to_be_Shifted[31]), .out(priority_encoder_1_out),
    .en_in(not_1_out));  // open: gs, en_out
  not not_1 (not_1_out, Cout);
  assign not_2_out = ~priority_encoder_1_out;  // NOT_Gate not_2, 5 bits wide
  Adder #(.width(5)) adder_1 (.a({5{1'b1}}), .b(not_2_out), .out(out_6), .cin(1'b1));  // open: cout
  Multiplexer #(.width(5), .enable("false")) multiplexer_1 (
    .in0(out_6), .in1(in_2), .out(multiplexer_1_out), .sel(Cout));
  Shifter #(.width(32)) shifter_1 (.in(Significand_to_be_Shifted), .\dist (multiplexer_1_out), .out(shifter_1_out));
  Shifter #(.width(32), .shift("lr")) shifter_2 (
    .in(Significand_to_be_Shifted), .\dist ({in_4, Cout}), .out(shifter_2_out));
  Multiplexer #(.width(32), .enable("false")) multiplexer_2 (
    .in0(shifter_1_out), .in1({1'b1, shifter_2_out[30:0]}), .out(Normalized_32_bit_Significand), .sel(Cout));

  // Notes on the sheet:
  //   Significand to be Shifted
  //   L.Shifter
  //   R.Shifter
endmodule
