// Logisim project Normalization of exponent.circ as structural Verilog: 1 circuit, main circuit exponent_normalization
module exponent_normalization (
  input  Cin_of_Final_Adder,
  input  [10:0] GREATER_OUTPUT_FROM_TASK1,
  input  [10:0] SHAMT_FROM_TASK5,
  output [10:0] EXP_RESULT,
  output OVERFLOW,
  output UNDERFLOW
);

  wire adder_1_cout, not_4_out;
  wire [10:0] adder_1_out, not_2_out, not_3_out;

  // NOT_Gate not_1 is placed but not wired
  assign not_2_out = ~SHAMT_FROM_TASK5;  // NOT_Gate not_2, 11 bits wide
  Adder #(.width(11)) adder_1 (
    .a(GREATER_OUTPUT_FROM_TASK1), .b(not_2_out), .out(adder_1_out), .cin(1'b1), .cout(adder_1_cout));
  assign not_3_out = ~adder_1_out;  // NOT_Gate not_3, 11 bits wide
  not not_4 (not_4_out, adder_1_cout);
  Adder #(.width(11)) adder_2 (
    .a({11{1'b0}}), .b(adder_1_out), .out(EXP_RESULT), .cin(Cin_of_Final_Adder));  // open: cout
  and and_1 (OVERFLOW, EXP_RESULT[0], EXP_RESULT[1], EXP_RESULT[2], EXP_RESULT[3], EXP_RESULT[4], EXP_RESULT[5], EXP_RESULT[6], EXP_RESULT[7], EXP_RESULT[8], EXP_RESULT[9], EXP_RESULT[10]);
  or or_1 (UNDERFLOW, not_3_out[0], not_3_out[1], not_3_out[2], not_3_out[3], not_3_out[4], not_3_out[5], not_3_out[6], not_3_out[7], not_3_out[8], not_3_out[9], not_3_out[10], not_4_out);
endmodule
