// Logisim project RoundingCkt.circ as structural Verilog: 1 circuit, main circuit Rounding Circuit
module Rounding_Circuit (
  input  [31:0] Normalized_32_bit_Significand,
  output [31:0] Rounded_32_bit_Significand,
  output Cout
);

  wire and_1_out, comparator_1_eq, comparator_1_gt, or_1_out;

  Comparator #(.width(11), .mode("unsigned")) comparator_1 (
    .a(Normalized_32_bit_Significand[10:0]), .b(11'h400), .gt(comparator_1_gt), .eq(comparator_1_eq));  // open: lt
  and and_1 (and_1_out, Normalized_32_bit_Significand[11], comparator_1_eq);
  or or_1 (or_1_out, and_1_out, comparator_1_gt);
  Adder #(.width(21)) adder_1 (
    .a(Normalized_32_bit_Significand[31:11]), .b({21{1'b0}}), .out(Rounded_32_bit_Significand[31:11]),
    .cin(or_1_out), .cout(Cout));

  assign Rounded_32_bit_Significand[10:0] = {11{1'b0}};

  // Notes on the sheet:
  //   1 << 10
endmodule
