// Logisim project SignificandAdder.circ as structural Verilog: 1 circuit, main circuit Significant Adder
module Significant_Adder (
  input  Sign_A,
  input  Sign_B,
  input  [31:0] frac_B,
  input  [31:0] frac_A,
  output [31:0] Significand_to_be_Shifted,
  output Cout
);

  wire and_1_out, not_1_out, xor_1_out;
  wire [31:0] adder_2_out, multiplexer_1_out, multiplexer_2_out, xor_2_out, xor_3_out;

  Multiplexer #(.width(32), .enable("false")) multiplexer_1 (
    .in0({32{1'b0}}), .in1({32{1'b1}}), .out(multiplexer_1_out), .sel(xor_1_out));
  xor xor_1 (xor_1_out, Sign_A, Sign_B);
  Adder #(.width(32)) adder_1 (
    .a({32{1'b0}}), .b(xor_3_out), .out(Significand_to_be_Shifted), .cin(and_1_out));  // open: cout
  assign xor_2_out = multiplexer_1_out ^ frac_B;  // XOR_Gate xor_2, 32 bits wide
  Adder #(.width(32)) adder_2 (.a(xor_2_out), .b(frac_A), .out(adder_2_out), .cin(xor_1_out), .cout(Cout));
  not not_1 (not_1_out, Cout);
  and and_1 (and_1_out, xor_1_out, not_1_out);
  Multiplexer #(.width(32), .enable("false")) multiplexer_2 (
    .in0({32{1'b0}}), .in1({32{1'b1}}), .out(multiplexer_2_out), .sel(and_1_out));
  assign xor_3_out = adder_2_out ^ multiplexer_2_out;  // XOR_Gate xor_3, 32 bits wide
endmodule
