// Logisim project exponentNormalization.circ as structural Verilog: 1 circuit, main circuit Exponent Normalization
module Exponent_Normalization (
  input  [31:0] NORMALIZED_32_BIT_SIGNIFICAND,
  input  Cin_of_Final_Adder,
  input  [10:0] GREATER_EXPONENT,
  input  [4:0] LEFT_SHAMT_FROM_FRACNORM,
  output [10:0] EXPONENT_RESULT,
  output OVERFLOW,
  output UNDERFLOW
);

  wire adder_1_cout, nor_1_out, nor_2_out, not_2_out;
  wire [10:0] adder_1_out, adder_2_out, bit_extender_1_out, not_1_out;

  assign bit_extender_1_out = {{6{1'b0}}, LEFT_SHAMT_FROM_FRACNORM};  // Bit_Extender bit_extender_1
  assign not_1_out = ~bit_extender_1_out;  // NOT_Gate not_1, 11 bits wide
  Adder #(.width(11)) adder_1 (.a(GREATER_EXPONENT), .b(not_1_out), .out(adder_1_out), .cin(1'b1), .cout(adder_1_cout));
  Adder #(.width(11)) adder_2 (
    .a({11{1'b0}}), .b(adder_1_out), .out(adder_2_out), .cin(Cin_of_Final_Adder));  // open: cout
  and and_1 (OVERFLOW, adder_2_out[0], adder_2_out[1], adder_2_out[2], adder_2_out[3], adder_2_out[4], adder_2_out[5], adder_2_out[6], adder_2_out[7], adder_2_out[8], adder_2_out[9], adder_2_out[10]);
  nor nor_1 (nor_1_out, adder_1_out[0], adder_1_out[1], adder_1_out[2], adder_1_out[3], adder_1_out[4], adder_1_out[5], adder_1_out[6], adder_1_out[7], adder_1_out[8], adder_1_out[9], adder_1_out[10]);
  not not_2 (not_2_out, adder_1_cout);
  nor nor_2 (nor_2_out, NORMALIZED_32_BIT_SIGNIFICAND[0], NORMALIZED_32_BIT_SIGNIFICAND[1], NORMALIZED_32_BIT_SIGNIFICAND[2], NORMALIZED_32_BIT_SIGNIFICAND[3], NORMALIZED_32_BIT_SIGNIFICAND[4], NORMALIZED_32_BIT_SIGNIFICAND[5], NORMALIZED_32_BIT_SIGNIFICAND[6], NORMALIZED_32_BIT_SIGNIFICAND[7], NORMALIZED_32_BIT_SIGNIFICAND[8], NORMALIZED_32_BIT_SIGNIFICAND[9], NORMALIZED_32_BIT_SIGNIFICAND[10], NORMALIZED_32_BIT_SIGNIFICAND[11], NORMALIZED_32_BIT_SIGNIFICAND[12], NORMALIZED_32_BIT_SIGNIFICAND[13], NORMALIZED_32_BIT_SIGNIFICAND[14], NORMALIZED_32_BIT_SIGNIFICAND[15], NORMALIZED_32_BIT_SIGNIFICAND[16], NORMALIZED_32_BIT_SIGNIFICAND[17], NORMALIZED_32_BIT_SIGNIFICAND[18], NORMALIZED_32_BIT_SIGNIFICAND[19], NORMALIZED_32_BIT_SIGNIFICAND[20], NORMALIZED_32_BIT_SIGNIFICAND[21], NORMALIZED_32_BIT_SIGNIFICAND[22], NORMALIZED_32_BIT_SIGNIFICAND[23], NORMALIZED_32_BIT_SIGNIFICAND[24], NORMALIZED_32_BIT_SIGNIFICAND[25], NORMALIZED_32_BIT_SIGNIFICAND[26], NORMALIZED_32_BIT_SIGNIFICAND[27], NORMALIZED_32_BIT_SIGNIFICAND[28], NORMALIZED_32_BIT_SIGNIFICAND[29], NORMALIZED_32_BIT_SIGNIFICAND[30], 1'b0);
  Multiplexer #(.width(11), .enable("false")) multiplexer_1 (
    .in0(adder_2_out), .in1({11{1'b0}}), .out(EXPONENT_RESULT), .sel(nor_2_out));
  or or_1 (UNDERFLOW, nor_1_out, not_2_out);
endmodule
